# Fritzing sketch schematic (saved by Fritzing 0.7.5b)
breadboards: 1

parts:
  Arduino1 = Arduino
  U1 = 74HC595 [package="DIP16 [THT]"]
  LED1 = LED - 5mm [color="Red (633nm)" package="5 mm [THT]"]
  LED2 = LED - 5mm [color="Red (633nm)" package="5 mm [THT]"]
  LED3 = LED - 5mm [color="Red (633nm)" package="5 mm [THT]"]
  LED4 = LED - 5mm [color="Red (633nm)" package="5 mm [THT]"]
  LED5 = LED - 5mm [color="Red (633nm)" package="5 mm [THT]"]
  LED6 = LED - 5mm [color="Red (633nm)" package="5 mm [THT]"]
  LED7 = LED - 5mm [color="Red (633nm)" package="5 mm [THT]"]
  LED8 = LED - 5mm [color="Red (633nm)" package="5 mm [THT]"]

nets:
  GND: Arduino1.GND, U1.GND, U1.OE, LED1.cathode, LED2.cathode, LED3.cathode, LED4.cathode, LED5.cathode, LED6.cathode, LED7.cathode, LED8.cathode
  N1: Arduino1.D5, U1.SH_CP
  N2: Arduino1.D4, U1.ST_CP
  N3: Arduino1.D3, U1.DS
  N4: Arduino1.IO_REF, U1.MR, U1.VCC
  N5: U1.Q1, LED2.anode
  N6: U1.Q2, LED3.anode
  N7: U1.Q3, LED4.anode
  N8: U1.Q4, LED5.anode
  N9: U1.Q5, LED6.anode
  N10: U1.Q6, LED7.anode
  N11: U1.Q7, LED8.anode
  N12: U1.Q0, LED1.anode
